# Fritzing sketch GestureBot Schematic (saved by Fritzing 0.9.3b)
breadboards: 1

parts:
  Servo_1 = Servo 6
  Servo_3 = Servo 1
  Servo_4 = Servo 1
  Servo_5 = Servo 1
  Servo_6 = Servo 1
  Servo_7 = Servo 1
  Servo_8 = Servo 1
  Servo_9 = Servo 1
  Servo_10 = Servo 1
  M1 = Stepper Motor - Bipolar  # not connected
  M2 = Stepper Motor - Bipolar  # not connected
  S1 = Pushbutton [package="[THT]"]
  C1 = Electrolytic Capacitor [capacitance=100μF package="0807 [SMD, electrolytic]"]
  C2 = Electrolytic Capacitor [capacitance=100μF package="0807 [SMD, electrolytic]"]
  C3 = Electrolytic Capacitor [capacitance=100μF package="0807 [SMD, electrolytic]"]
  C4 = Electrolytic Capacitor [capacitance=100μF package="0807 [SMD, electrolytic]"]
  C5 = Electrolytic Capacitor [capacitance=100μF package="0807 [SMD, electrolytic]"]
  C6 = Electrolytic Capacitor [capacitance=100μF package="0807 [SMD, electrolytic]"]
  C7 = Electrolytic Capacitor [capacitance=100μF package="0807 [SMD, electrolytic]"]
  C8 = Electrolytic Capacitor [capacitance=100μF package="0807 [SMD, electrolytic]"]
  C9 = Electrolytic Capacitor [capacitance=100μF package="0807 [SMD, electrolytic]"]
  C10 = Electrolytic Capacitor [capacitance=100μF package="0807 [SMD, electrolytic]"]
  Servo_2 = Servo 6
  R1 = Resistor [tolerance=±5% resistance=10k package=THT]
  Part1 = Arduino Mega 2560 (Rev3)
  BAT1 = BC9VPC [package=bc9vpc]
  Q1 = TRANSISTOR_NPN [package=to-92-ammo]
  Q2 = TRANSISTOR_NPN [package=to-92-ammo]

nets:
  GND: Servo_1.gnd, Servo_3.gnd, Servo_4.gnd, Servo_5.gnd, Servo_6.gnd, Servo_7.gnd, Servo_8.gnd, Servo_9.gnd, Servo_10.gnd, C1.-, C2.-, C3.-, C4.-, C5.-, C6.-, C7.-, C8.-, C9.-, C10.-, Servo_2.gnd, R1.Pin_0, Part1.GND, BAT1.V-, Q1.C, Q2.C
  VCC: Servo_1.vcc, Servo_5.vcc, Servo_6.vcc, Servo_9.vcc, C1.+, C2.+, C3.+, C4.+, C5.+, Servo_2.vcc
  N1: Servo_1.pulse, Part1.D2_PWM
  VCC_2: Servo_3.vcc, Servo_4.vcc, Servo_7.vcc, Servo_8.vcc, Servo_10.vcc, C6.+, C7.+, C8.+, C9.+, C10.+
  N2: Servo_3.pulse, Part1.D4_PWM
  N3: Servo_4.pulse, Part1.D5_PWM
  N4: Servo_5.pulse, Part1.D6_PWM
  N5: Servo_6.pulse, Part1.D8_PWM
  N6: Servo_7.pulse, Part1.D7_PWM
  N7: Servo_8.pulse, Part1.D9_PWM
  N8: Servo_9.pulse, Part1.D10_PWM
  N9: Servo_10.pulse, Part1.D11_PWM
  N10: S1.Pin_1, S1.Pin_2, Part1.5V
  N11: S1.Pin_3, S1.Pin_4, R1.Pin_1, Part1.D22
  N12: Servo_2.pulse, Part1.D3_PWM
  N13: Part1.D13_PWM, Q2.B
  N14: Part1.D12_PWM, Q1.B

custom parts:
  Servo 6: A generic servo.
  Servo 1: A generic servo.
